# Fritzing sketch circuit (saved by Fritzing 0.9.6b)
circuit board: 8.46667cm x 5.64444cm

parts:
  U1 = ESP32-38PinWide [part_number=ESP32-38PinWide]
  Display1 = LCD screen 16x2 IIC [part_number=101290]
  S_start = Round Pushbutton
  S_reset = Square Pushbutton
  SERVO1 = Tower Pro SG90 servo [part_number=101246]
  HC-SR04_Sensor_1 = HC-SR04 Ultrasonic Distance Sensor
  Part1 = KY-037 High Sensitivity Sound Detection Module [package="Breakout board"]
  R1 = Resistor [tolerance=±5% resistance=220 package="0805 [SMD]"]

nets:
  N1: U1.3.3, HC-SR04_Sensor_1.VCC, Part1.+, R1.Pin_1
  N2: U1.GPIO33, SERVO1.Signal
  N3: U1.GPIO25, Display1.GND, Part1.G
  GND: U1.GND, SERVO1.GND, HC-SR04_Sensor_1.GND
  VIN: U1.VIN, Display1.VCC, SERVO1.+5V
  N4: U1.GPIO0, S_start.leg1
  N5: U1.GPIO4, S_reset.leg0
  N6: U1.GPIO16, Part1.D0
  N7: U1.GPIO5, HC-SR04_Sensor_1.TRIG
  N8: U1.GPIO18, HC-SR04_Sensor_1.ECHO
  N9: U1.GPIO21, Display1.SDA
  N10: U1.GPIO22, Display1.SCL
  N11: S_start.leg0, S_reset.leg1, R1.Pin_0

custom parts:
  ESP32-38PinWide: Generic 38-Pin ESP32 with wide format (only access to one side of pins on a breadboard) based on Stephen Lilley's HiLetgo ESP-WROOM-32 ESP32 ESP-32S Development Board.
  LCD screen 16x2 IIC: LCD screen with HD44780 controller enables showing text, symbols, value or anything else that comes from Croduino/Arduino. It is capable of showing 16 symbols in two lines and therefore can be used in many projects that need to send clearly visible and legible output information.. • Color of symbols: White • Backlight: Blue • Dimensions: 80 x 36 x 12 mm • Screen dimensions: 64.5 x 16 mm •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
  Tower Pro SG90 servo: Original file by John De Cristofaro http://www.adafruit.com/products/1449 Adafruit Feedback Servo (Small) Edited by: e-radionica.com 28/9/2015
  KY-037 High Sensitivity Sound Detection Module: KY-037 high sensitivity sound detection module is an analog/digital sensor that uses a condenser microphone to observe changes in environment noise.
