# Fritzing sketch skema (saved by Fritzing 0.9.6b)
breadboards: 2

parts:
  Display2 = LCD screen 16x2 IIC [part_number=101290]
  Part2 = KY-037 High Sensitivity Sound Detection Module [package="Breakout board"]
  HC-SR04_Sensor_2 = HC-SR04 Ultrasonic Distance Sensor
  SERVO2 = Tower Pro SG90 servo [part_number=101246]
  U1 = ESP32-38PinWide [part_number=ESP32-38PinWide]
  Start = Pushbutton [package="[THT]"]
  Reset = Pushbutton [package="[THT]"]
  R1 = Resistor [tolerance=±5% power=0.25 resistance=220 package=THT]

nets:
  GND: Display2.GND, Part2.G, HC-SR04_Sensor_2.GND, SERVO2.GND, U1.GND
  VCC: Display2.VCC, SERVO2.+5V, U1.VIN
  N1: Display2.SDA, U1.GPIO21
  N2: Display2.SCL, U1.GPIO22
  N3: Part2.+, HC-SR04_Sensor_2.VCC, U1.3.3, R1.Pin_0
  N4: Part2.D0, U1.GPIO16
  N5: HC-SR04_Sensor_2.TRIG, U1.GPIO5
  N6: HC-SR04_Sensor_2.ECHO, U1.GPIO18
  N7: SERVO2.Signal, U1.GPIO33
  N8: U1.GPIO0, Start.Pin_4
  N9: U1.GPIO4, Reset.Pin_4
  N10: Start.Pin_1, Start.Pin_2, R1.Pin_1

custom parts:
  LCD screen 16x2 IIC: LCD screen with HD44780 controller enables showing text, symbols, value or anything else that comes from Croduino/Arduino. It is capable of showing 16 symbols in two lines and therefore can be used in many projects that need to send clearly visible and legible output information.. • Color of symbols: White • Backlight: Blue • Dimensions: 80 x 36 x 12 mm • Screen dimensions: 64.5 x 16 mm •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
  KY-037 High Sensitivity Sound Detection Module: KY-037 high sensitivity sound detection module is an analog/digital sensor that uses a condenser microphone to observe changes in environment noise.
  Tower Pro SG90 servo: Original file by John De Cristofaro http://www.adafruit.com/products/1449 Adafruit Feedback Servo (Small) Edited by: e-radionica.com 28/9/2015
  ESP32-38PinWide: Generic 38-Pin ESP32 with wide format (only access to one side of pins on a breadboard) based on Stephen Lilley's HiLetgo ESP-WROOM-32 ESP32 ESP-32S Development Board.
